# Fritzing sketch board (saved by Fritzing 0.9.1b)
breadboards: 1

parts:
  Part1 = Arduino Uno (Rev3) - ICSP
  LED1 = smd LED [color="Red (633nm)" package="0603 [SMD]"]
  LED2 = smd LED [color="Yellow (585nm)" package="0603 [SMD]"]
  LED3 = smd LED [color="Green (560nm)" package="0603 [SMD]"]
  U1 = POT [package=trim_pot]
  S2 = Pushbutton [package="[THT]"]
  R2 = Resistor [tolerance=±5% resistance=220 package="0603 [SMD]"]
  R3 = Resistor [tolerance=±5% resistance=220 package="0603 [SMD]"]
  R4 = Resistor [tolerance=±5% resistance=220 package="0603 [SMD]"]
  S3 = Pushbutton [package="[THT]"]
  R5 = Resistor [tolerance=±5% resistance=220 package="0603 [SMD]"]
  R6 = Resistor [tolerance=±5% resistance=220 package="0603 [SMD]"]

nets:
  N1: Part1.A0, Part1.GND, LED1.anode, LED2.anode, LED3.anode, U1.E, R5.Pin_0, R6.Pin_0
  N2: Part1.D8, Part1.D9_PWM, Part1.5V, U1.S, U1.A, S2.Pin_1, S2.Pin_2, S2.Pin_3, S2.Pin_4, S3.Pin_1, S3.Pin_2, S3.Pin_3, S3.Pin_4, R5.Pin_1, R6.Pin_1
  N3: Part1.D3_PWM, LED3.cathode, R3.Pin_0, R3.Pin_1
  N4: Part1.D4, LED2.cathode, R2.Pin_0, R2.Pin_1
  N5: Part1.D5_PWM, LED1.cathode, R4.Pin_0, R4.Pin_1
